# Fritzing sketch wind tunnel (saved by Fritzing 0.9.3b)
circuit board: 8.64738cm x 5.46882cm
breadboards: 1

parts:
  1 = Arduino Uno (Rev3)
  IC2 = L293D [package=THT]
  U5 = TMP102 [package=sot563]
  M1 = DC Motor
  R1 = Resistor [tolerance=±5% resistance=10k package=THT]
  R2 = Resistor [tolerance=±5% resistance=10k package=THT]
  Power_plug1 = Power plug

nets:
  N1: 1.A4/SDA, U5.SDA, R1.Pin_0
  N2: 1.A5/SCL, U5.SCL, R2.Pin_0
  N3: 1.D9_PWM, IC2.In_1
  5V: 1.5V, IC2.+V, U5.VCC, R1.Pin_1, R2.Pin_1, Power_plug1.VCC
  GND: 1.GND, IC2.0V, U5.GND, Power_plug1.GND
  N4: IC2.Out_1_(_Controlled_by_Enable_1_), M1.pin_2
  N5: IC2.Out_2_(_Controlled_by_Enable_1_), M1.pin_1
  12V: IC2.+Vmotor
